# Fritzing sketch led-pid (saved by Fritzing 0.7.11b)
breadboards: 1

parts:
  A = Arduino
  Photo_Resistor = Photocell (LDR) [package=THT]
  10kΩ = Resistor [tolerance=±5% resistance=10k package=THT]
  LED = LED - 5mm [color="Red (633nm)" package="5 mm [THT]"]
  330Ω = Resistor [tolerance=±5% resistance=330 package=THT]
  10kΩ_2 = Rotary Potentiometer (Small) [maximum_resistance=10kΩ]

nets:
  N1: A.GND, 10kΩ.Pin_1, 330Ω.Pin_1, 10kΩ_2.leg1
  N2: A.D9, LED.anode
  N3: A.+5V, Photo_Resistor.pin_0, 10kΩ_2.leg2
  N4: A.A0, Photo_Resistor.pin_1, 10kΩ.Pin_0
  N5: A.A1, 10kΩ_2.wiper
  N6: LED.cathode, 330Ω.Pin_0
