# Fritzing sketch pot-fade (saved by Fritzing 0.7.11b)
breadboards: 1

parts:
  Arduino1 = Arduino
  330Ω = Resistor [tolerance=±5% resistance=330 package=THT]
  LED1 = LED - 5mm [color="Red (633nm)" package="5 mm [THT]"]
  10kΩ = Rotary Potentiometer (Small) [maximum_resistance=100kΩ]

nets:
  N1: Arduino1.GND, 330Ω.Pin_0, 10kΩ.leg1
  N2: Arduino1.D9, LED1.anode
  N3: Arduino1.+5V, 10kΩ.leg2
  N4: Arduino1.A0, 10kΩ.wiper
  N5: 330Ω.Pin_1, LED1.cathode
