# Fritzing sketch serial_switch (saved by Fritzing 0.7.11b)
breadboards: 1

parts:
  Arduino1 = Arduino
  R1 = Resistor [tolerance=±5% resistance=220 package=THT]
  R2 = Resistor [tolerance=±5% resistance=220 package=THT]
  LED2 = LED - 5mm [color="Red (633nm)" package="5 mm [THT]"]
  LED1 = LED - 5mm [color="Red (633nm)" package="5 mm [THT]"]

nets:
  N1: Arduino1.D10, LED2.anode
  N2: Arduino1.D9, LED1.anode
  N3: Arduino1.GND, R1.Pin_0, R2.Pin_0
  N4: R1.Pin_1, LED2.cathode
  N5: R2.Pin_1, LED1.cathode
