# Fritzing sketch temp (saved by Fritzing 0.7.11b)
breadboards: 1

parts:
  Arduino1 = Arduino
  T1 = LM35 Temperature Sensor [package="TO92 [THT]"]
  LED = LED - 5mm [color="Red (633nm)" package="5 mm [THT]"]
  330Ω = Resistor [tolerance=±5% resistance=330 package=THT]
  10kΩ = Rotary Potentiometer (Large) [maximum_resistance=10kΩ package=THT]

nets:
  N1: Arduino1.D9, 330Ω.Pin_1
  N2: Arduino1.+5V, T1.+Vs, 10kΩ.leg2
  GND: Arduino1.GND, T1.GND, LED.cathode, 10kΩ.leg1
  N3: Arduino1.A0, 10kΩ.wiper
  N4: Arduino1.A1, T1.Vout
  N5: LED.anode, 330Ω.Pin_0
